# Fritzing sketch navibot-arduino-fritzing (saved by Fritzing 0.9.2b)
circuit board: 5.66019cm x 5.18091cm
breadboards: 1

parts:
  Teensyduino = Teensy 2.0
  DS1307_clock = Real Time Clock Module - DS1307 RTC Breakout Board
  IR_LED = LEDs [package=led10mm]
  R1 = Resistor [tolerance=±5% resistance=220 package=THT]

nets:
  GND: Teensyduino.GND, DS1307_clock.GND, IR_LED.C
  N1: Teensyduino.D0, DS1307_clock.SCL
  N2: Teensyduino.D1, DS1307_clock.SDA
  N3: Teensyduino.C7, R1.Pin_0
  5V: Teensyduino.VCC, DS1307_clock.5V
  N4: IR_LED.A, R1.Pin_1
